// Logisim project CPU_DEF.circ as structural Verilog: 26 circuits, main circuit CPU
module CPU (
  input  in_1,
  input  in_2,
  input  in_3,
  input  [7:0] in_4,
  output [7:0] REG_0,
  output [7:0] REG_1,
  output [7:0] REG_2,
  output [7:0] REG_3,
  output [7:0] ADDRESS,
  output [7:0] DATA_IN,
  output [7:0] IAR,
  output [7:0] out_12,
  output [7:0] DATA_OUT
);

  wire AL_FLAG, alu_1_carry_out, alu_1_equal, alu_1_larger, alu_1_zero, C_FLAG, clock_1_out,
       control_unit_1_acc_e, control_unit_1_bus_1, control_unit_1_ir_s, control_unit_1_out_6,
       control_unit_1_out_8, control_unit_1_out_11, control_unit_1_out_12, control_unit_1_r0_e,
       control_unit_1_r0_s, control_unit_1_r1_e, control_unit_1_r1_s, control_unit_1_r2_e,
       control_unit_1_r2_s, control_unit_1_r3_e, control_unit_1_r3_s, control_unit_1_ram_e,
       control_unit_1_ram_s, control_unit_1_set_flag, cpu_clock_1_clk, cpu_clock_1_clke, cpu_clock_1_clks,
       EQ_FLAG, Z_FLAG;
  wire [7:0] alu_1_out_7, cpu_accum_1_o, cpu_bus_1_1_o, cpu_ir_1_o, cpu_temp_1_o;

  CPU_TEMP cpu_temp_1 (.i(cpu_accum_1_o), .s(control_unit_1_out_12), .o(cpu_temp_1_o));
  CPU_BUS_1 cpu_bus_1_1 (.i(cpu_temp_1_o), .bus_1_a6cd2c94(control_unit_1_bus_1), .o(cpu_bus_1_1_o));
  ALU alu_1 (
    .in_3(C_FLAG), .in_1(cpu_accum_1_o), .in_2(cpu_bus_1_1_o), .in_4(in_1), .in_5(in_2), .in_6(in_3),
    .larger(alu_1_larger), .equal(alu_1_equal), .out_7(alu_1_out_7), .carry_out(alu_1_carry_out),
    .zero(alu_1_zero));  // open: out_8
  CPU_ACCUM cpu_accum_1 (
    .i(alu_1_out_7), .s(control_unit_1_out_8), .e(control_unit_1_acc_e), .ACC(out_12), .o(cpu_accum_1_o));
  FLAGS_REG flags_reg_1 (
    .in_5(control_unit_1_set_flag), .in_3(alu_1_equal), .in_4(alu_1_zero), .in_1(alu_1_carry_out),
    .in_2(alu_1_larger), .out_7(AL_FLAG), .out_8(EQ_FLAG), .out_9(Z_FLAG), .out_6(C_FLAG));
  Clock clock_1 (.out(clock_1_out));
  CPU_CLOCK cpu_clock_1 (.CLKIN(clock_1_out), .CLK(cpu_clock_1_clk), .CLKE(cpu_clock_1_clke), .CLKS(cpu_clock_1_clks));
  CPU_REG cpu_reg_1 (
    .i(cpu_accum_1_o), .s(control_unit_1_r0_s), .e(control_unit_1_r0_e), .\reg (REG_0), .o(cpu_accum_1_o));
  CPU_REG cpu_reg_2 (.i(cpu_accum_1_o), .s(1'b1), .e(control_unit_1_out_11), .\reg (IAR), .o(cpu_accum_1_o));
  CPU_REG cpu_reg_3 (
    .i(cpu_accum_1_o), .s(control_unit_1_r1_s), .e(control_unit_1_r1_e), .\reg (REG_1), .o(cpu_accum_1_o));
  CPU_REG cpu_reg_4 (
    .i(cpu_accum_1_o), .s(control_unit_1_r2_s), .e(control_unit_1_r2_e), .\reg (REG_2), .o(cpu_accum_1_o));
  CPU_IR cpu_ir_1 (.i(cpu_accum_1_o), .s(control_unit_1_ir_s), .o(cpu_ir_1_o));
  CPU_REG cpu_reg_5 (
    .i(cpu_accum_1_o), .s(control_unit_1_r3_s), .e(control_unit_1_r3_e), .\reg (REG_3), .o(cpu_accum_1_o));
  CONTROL_UNIT control_unit_1 (
    .in_1(cpu_clock_1_clks), .in_2(cpu_clock_1_clk), .in_3(cpu_clock_1_clke), .in_4(cpu_ir_1_o),
    .out_6(control_unit_1_out_6), .out_8(control_unit_1_out_8), .RAM_S(control_unit_1_ram_s),
    .out_12(control_unit_1_out_12), .R0_S(control_unit_1_r0_s), .R1_S(control_unit_1_r1_s),
    .R2_S(control_unit_1_r2_s), .R3_S(control_unit_1_r3_s), .IR_S(control_unit_1_ir_s),
    .RAM_E(control_unit_1_ram_e), .ACC_E(control_unit_1_acc_e), .out_11(control_unit_1_out_11),
    .R0_E(control_unit_1_r0_e), .R1_E(control_unit_1_r1_e), .R2_E(control_unit_1_r2_e),
    .R3_E(control_unit_1_r3_e), .BUS_1(control_unit_1_bus_1), .Z_FLAG(Z_FLAG), .C_FLAG(C_FLAG),
    .AL_FLAG(AL_FLAG), .EQ_FLAG(EQ_FLAG), .SET_FLAG(control_unit_1_set_flag));  // open: IAR_S
  MEM_RAM_256BYTES mem_ram_256bytes_1 (
    .in_4(control_unit_1_ram_s), .in_5(control_unit_1_ram_e), .RAM_IN(in_4), .RAM_ADDR_IN(cpu_accum_1_o),
    .in_2(control_unit_1_out_6), .RAM_OUT(cpu_accum_1_o), .RAM_OUT_FLG(DATA_OUT), .RAM_IN_FLG(DATA_IN),
    .RAM_ADDR_FLG(ADDRESS));  // open: in_6, out_61, out_77, out_93, out_109, out_125, out_13, out_29, out_45, out_141, out_157, out_173, out_189, out_205, out_221, out_237, out_253, out_62, out_78, out_94, out_110, out_126, out_14, out_30, out_46, out_142, out_158, out_174, out_190, out_206, out_222, out_238, out_254, out_63, out_79, out_95, out_111, out_127, out_15, out_31, out_47, out_143, out_159, out_175, out_191, out_207, out_223, out_239, out_255, out_64, out_80, out_96, out_112, out_128, out_16, out_32, out_48, out_144, out_160, out_176, out_192, out_208, out_224, out_240, out_256, out_65, out_81, out_97, out_113, out_129, out_17, out_33, out_49, out_145, out_161, out_177, out_193, out_209, out_225, out_241, out_257, out_66, out_82, out_98, out_114, out_130, out_18, out_34, out_50, out_146, out_162, out_178, out_194, out_210, out_226, out_242, out_258, out_67, out_83, out_99, out_115, out_131, out_19, out_35, out_51, out_147, out_163, out_179, out_195, out_211, out_227, out_243, out_259, out_68, out_84, out_100, out_116, out_132, out_20, out_36, out_52, out_148, out_164, out_180, out_196, out_212, out_228, out_244, out_260, out_69, out_85, out_101, out_117, out_133, out_21, out_37, out_53, out_149, out_165, out_181, out_197, out_213, out_229, out_245, out_261, out_70, out_86, out_102, out_118, out_134, out_22, out_38, out_54, out_150, out_166, out_182, out_198, out_214, out_230, out_246, out_262, out_71, out_87, out_103, out_119, out_135, out_23, out_39, out_55, out_151, out_167, out_183, out_199, out_215, out_231, out_247, out_263, out_72, out_88, out_104, out_120, out_136, out_24, out_40, out_56, out_152, out_168, out_184, out_200, out_216, out_232, out_248, out_264, out_73, out_89, out_105, out_121, out_137, out_25, out_41, out_57, out_153, out_169, out_185, out_201, out_217, out_233, out_249, out_265, out_74, out_90, out_106, out_122, out_138, out_26, out_42, out_58, out_154, out_170, out_186, out_202, out_218, out_234, out_250, out_266, out_59, out_75, out_91, out_107, out_123, out_11, out_27, out_43, out_139, out_155, out_171, out_187, out_203, out_219, out_235, out_251, out_60, out_76, out_92, out_108, out_124, out_12, out_28, out_44, out_140, out_156, out_172, out_188, out_204, out_220, out_236, out_252
endmodule

module CONTROL_UNIT (
  input  in_1,
  input  in_2,
  input  in_3,
  input  [7:0] in_4,
  output BUS_1,
  output out_6,
  output RAM_E,
  output out_8,
  output ACC_E,
  output RAM_S,
  output out_11,
  output out_12,
  output R0_S,
  output R0_E,
  output R1_S,
  output R1_E,
  output R2_S,
  output R2_E,
  output R3_S,
  output R3_E,
  output IR_S,
  output IAR_S,
  output C_FLAG,
  output AL_FLAG,
  output EQ_FLAG,
  output Z_FLAG,
  output SET_FLAG
);

  wire cntrl_u_stepper_1_out_4, cntrl_u_stepper_1_out_5, cntrl_u_stepper_1_out_8, cntrl_u_stepper_1_out_9;

  and and_1 (RAM_E, in_3, cntrl_u_stepper_1_out_4);
  and and_2 (ACC_E, in_3, cntrl_u_stepper_1_out_5);
  and and_3 (out_11, in_3, BUS_1);
  and and_4 (R0_E, in_3, 1'b0);
  and and_5 (R1_E, in_3, 1'b0);
  and and_6 (R2_E, in_3, 1'b0);
  and and_7 (R3_E, in_3, 1'b0);
  CNTRL_U_STEPPER cntrl_u_stepper_1 (
    .in_2(in_2), .in_1(cntrl_u_stepper_1_out_9), .out_5(cntrl_u_stepper_1_out_5),
    .out_8(cntrl_u_stepper_1_out_8), .out_9(cntrl_u_stepper_1_out_9), .out_3(BUS_1),
    .out_4(cntrl_u_stepper_1_out_4));  // open: out_6, out_7
  and and_8 (out_6, in_1, BUS_1);
  and and_9 (out_8, in_1, BUS_1);
  and and_10 (RAM_S, in_1, 1'b0);
  and and_11 (out_12, in_1, 1'b0);
  and and_12 (R0_S, in_1, 1'b0);
  and and_13 (R1_S, in_1, 1'b0);
  and and_14 (R2_S, in_1, 1'b0);
  and and_15 (R3_S, in_1, cntrl_u_stepper_1_out_8);
  and and_16 (IR_S, in_1, cntrl_u_stepper_1_out_4);
  and and_17 (IAR_S, in_1, cntrl_u_stepper_1_out_5);

  // Notes on the sheet:
  //   IAR_E
  //   CLKS
  //   CLK
  //   CLKE
  //   IR_IN
  //   MAR_S
  //   ACC_S
  //   TMP_S
endmodule

module ALU (
  input  [7:0] in_1,
  input  [7:0] in_2,
  input  in_3,
  input  in_4,
  input  in_5,
  input  in_6,
  output [7:0] out_7,
  output out_8,
  output larger,
  output zero,
  output equal,
  output carry_out
);

  wire alu_adder_8_1_out_5, alu_shift_left_1_out_4, alu_shift_right_1_shift_out, and_2_out, and_3_out,
       and_4_out;
  wire [7:0] alu_adder_8_1_out_4, alu_dec_3_8_1_o, alu_le_comp_8_1_out_3, alu_shift_left_1_o,
       alu_shift_right_1_o, and_1_out, mem_enable_8_1_out_3, not_1_out, or_1_out;

  ALU_LE_COMP_8 alu_le_comp_8_1 (.in_2(in_2), .a(in_1), .equal(equal), .larger(larger), .out_3(alu_le_comp_8_1_out_3));
  assign or_1_out = in_1 | in_2;  // OR_Gate or_1, 8 bits wide
  assign and_1_out = in_1 & in_2;  // AND_Gate and_1, 8 bits wide
  assign not_1_out = ~in_1;  // NOT_Gate not_1, 8 bits wide
  ALU_SHIFT_LEFT alu_shift_left_1 (
    .in_2(in_1), .SHIFT_IN(in_3), .out_4(alu_shift_left_1_out_4), .o(alu_shift_left_1_o));
  ALU_ADDER_8 alu_adder_8_1 (
    .in_1(in_1), .in_2(in_2), .in_3(in_3), .out_4(alu_adder_8_1_out_4), .out_5(alu_adder_8_1_out_5));
  ALU_SHIFT_RIGHT alu_shift_right_1 (
    .in_1(in_1), .in_2(in_3), .SHIFT_OUT(alu_shift_right_1_shift_out), .o(alu_shift_right_1_o));
  MEM_ENABLE_8 mem_enable_8_1 (.in_2(alu_dec_3_8_1_o[6]), .in_1(alu_le_comp_8_1_out_3), .out_3(mem_enable_8_1_out_3));
  MEM_ENABLE_8 mem_enable_8_2 (.in_2(alu_dec_3_8_1_o[5]), .in_1(or_1_out), .out_3(out_7));
  MEM_ENABLE_8 mem_enable_8_3 (.in_2(alu_dec_3_8_1_o[4]), .in_1(and_1_out), .out_3(out_7));
  MEM_ENABLE_8 mem_enable_8_4 (.in_2(alu_dec_3_8_1_o[3]), .in_1(not_1_out), .out_3(out_7));
  MEM_ENABLE_8 mem_enable_8_5 (.in_2(alu_dec_3_8_1_o[2]), .in_1(alu_shift_left_1_o), .out_3(out_7));
  MEM_ENABLE_8 mem_enable_8_6 (.in_2(alu_dec_3_8_1_o[1]), .in_1(alu_shift_right_1_o), .out_3(out_7));
  MEM_ENABLE_8 mem_enable_8_7 (.in_2(alu_dec_3_8_1_o[0]), .in_1(alu_adder_8_1_out_4), .out_3(out_7));
  and and_2 (and_2_out, alu_shift_left_1_out_4, alu_dec_3_8_1_o[2]);
  and and_3 (and_3_out, alu_shift_right_1_shift_out, alu_dec_3_8_1_o[1]);
  and and_4 (and_4_out, alu_adder_8_1_out_5, alu_dec_3_8_1_o[0]);
  ALU_DEC_3_8 alu_dec_3_8_1 (.c(in_6), .b(in_5), .a(in_4), .o(alu_dec_3_8_1_o));
  assign carry_out = alu_dec_3_8_1_o[2] ? and_2_out : 1'bz;  // Controlled_Buffer controlled_buffer_1
  assign carry_out = alu_dec_3_8_1_o[1] ? and_3_out : 1'bz;  // Controlled_Buffer controlled_buffer_2
  assign carry_out = alu_dec_3_8_1_o[0] ? and_4_out : 1'bz;  // Controlled_Buffer controlled_buffer_3
  ALU_ZERO alu_zero_1 (.i(mem_enable_8_1_out_3), .o(zero));
endmodule

module MEM_RAM_256BYTES (
  input  [7:0] RAM_ADDR_IN,
  input  in_2,
  input  [7:0] RAM_IN,
  input  in_4,
  input  in_5,
  input  in_6,
  output [7:0] RAM_ADDR_FLG,
  output [7:0] RAM_IN_FLG,
  output [7:0] RAM_OUT_FLG,
  output [7:0] RAM_OUT,
  output [7:0] out_11,
  output [7:0] out_12,
  output [7:0] out_13,
  output [7:0] out_14,
  output [7:0] out_15,
  output [7:0] out_16,
  output [7:0] out_17,
  output [7:0] out_18,
  output [7:0] out_19,
  output [7:0] out_20,
  output [7:0] out_21,
  output [7:0] out_22,
  output [7:0] out_23,
  output [7:0] out_24,
  output [7:0] out_25,
  output [7:0] out_26,
  output [7:0] out_27,
  output [7:0] out_28,
  output [7:0] out_29,
  output [7:0] out_30,
  output [7:0] out_31,
  output [7:0] out_32,
  output [7:0] out_33,
  output [7:0] out_34,
  output [7:0] out_35,
  output [7:0] out_36,
  output [7:0] out_37,
  output [7:0] out_38,
  output [7:0] out_39,
  output [7:0] out_40,
  output [7:0] out_41,
  output [7:0] out_42,
  output [7:0] out_43,
  output [7:0] out_44,
  output [7:0] out_45,
  output [7:0] out_46,
  output [7:0] out_47,
  output [7:0] out_48,
  output [7:0] out_49,
  output [7:0] out_50,
  output [7:0] out_51,
  output [7:0] out_52,
  output [7:0] out_53,
  output [7:0] out_54,
  output [7:0] out_55,
  output [7:0] out_56,
  output [7:0] out_57,
  output [7:0] out_58,
  output [7:0] out_59,
  output [7:0] out_60,
  output [7:0] out_61,
  output [7:0] out_62,
  output [7:0] out_63,
  output [7:0] out_64,
  output [7:0] out_65,
  output [7:0] out_66,
  output [7:0] out_67,
  output [7:0] out_68,
  output [7:0] out_69,
  output [7:0] out_70,
  output [7:0] out_71,
  output [7:0] out_72,
  output [7:0] out_73,
  output [7:0] out_74,
  output [7:0] out_75,
  output [7:0] out_76,
  output [7:0] out_77,
  output [7:0] out_78,
  output [7:0] out_79,
  output [7:0] out_80,
  output [7:0] out_81,
  output [7:0] out_82,
  output [7:0] out_83,
  output [7:0] out_84,
  output [7:0] out_85,
  output [7:0] out_86,
  output [7:0] out_87,
  output [7:0] out_88,
  output [7:0] out_89,
  output [7:0] out_90,
  output [7:0] out_91,
  output [7:0] out_92,
  output [7:0] out_93,
  output [7:0] out_94,
  output [7:0] out_95,
  output [7:0] out_96,
  output [7:0] out_97,
  output [7:0] out_98,
  output [7:0] out_99,
  output [7:0] out_100,
  output [7:0] out_101,
  output [7:0] out_102,
  output [7:0] out_103,
  output [7:0] out_104,
  output [7:0] out_105,
  output [7:0] out_106,
  output [7:0] out_107,
  output [7:0] out_108,
  output [7:0] out_109,
  output [7:0] out_110,
  output [7:0] out_111,
  output [7:0] out_112,
  output [7:0] out_113,
  output [7:0] out_114,
  output [7:0] out_115,
  output [7:0] out_116,
  output [7:0] out_117,
  output [7:0] out_118,
  output [7:0] out_119,
  output [7:0] out_120,
  output [7:0] out_121,
  output [7:0] out_122,
  output [7:0] out_123,
  output [7:0] out_124,
  output [7:0] out_125,
  output [7:0] out_126,
  output [7:0] out_127,
  output [7:0] out_128,
  output [7:0] out_129,
  output [7:0] out_130,
  output [7:0] out_131,
  output [7:0] out_132,
  output [7:0] out_133,
  output [7:0] out_134,
  output [7:0] out_135,
  output [7:0] out_136,
  output [7:0] out_137,
  output [7:0] out_138,
  output [7:0] out_139,
  output [7:0] out_140,
  output [7:0] out_141,
  output [7:0] out_142,
  output [7:0] out_143,
  output [7:0] out_144,
  output [7:0] out_145,
  output [7:0] out_146,
  output [7:0] out_147,
  output [7:0] out_148,
  output [7:0] out_149,
  output [7:0] out_150,
  output [7:0] out_151,
  output [7:0] out_152,
  output [7:0] out_153,
  output [7:0] out_154,
  output [7:0] out_155,
  output [7:0] out_156,
  output [7:0] out_157,
  output [7:0] out_158,
  output [7:0] out_159,
  output [7:0] out_160,
  output [7:0] out_161,
  output [7:0] out_162,
  output [7:0] out_163,
  output [7:0] out_164,
  output [7:0] out_165,
  output [7:0] out_166,
  output [7:0] out_167,
  output [7:0] out_168,
  output [7:0] out_169,
  output [7:0] out_170,
  output [7:0] out_171,
  output [7:0] out_172,
  output [7:0] out_173,
  output [7:0] out_174,
  output [7:0] out_175,
  output [7:0] out_176,
  output [7:0] out_177,
  output [7:0] out_178,
  output [7:0] out_179,
  output [7:0] out_180,
  output [7:0] out_181,
  output [7:0] out_182,
  output [7:0] out_183,
  output [7:0] out_184,
  output [7:0] out_185,
  output [7:0] out_186,
  output [7:0] out_187,
  output [7:0] out_188,
  output [7:0] out_189,
  output [7:0] out_190,
  output [7:0] out_191,
  output [7:0] out_192,
  output [7:0] out_193,
  output [7:0] out_194,
  output [7:0] out_195,
  output [7:0] out_196,
  output [7:0] out_197,
  output [7:0] out_198,
  output [7:0] out_199,
  output [7:0] out_200,
  output [7:0] out_201,
  output [7:0] out_202,
  output [7:0] out_203,
  output [7:0] out_204,
  output [7:0] out_205,
  output [7:0] out_206,
  output [7:0] out_207,
  output [7:0] out_208,
  output [7:0] out_209,
  output [7:0] out_210,
  output [7:0] out_211,
  output [7:0] out_212,
  output [7:0] out_213,
  output [7:0] out_214,
  output [7:0] out_215,
  output [7:0] out_216,
  output [7:0] out_217,
  output [7:0] out_218,
  output [7:0] out_219,
  output [7:0] out_220,
  output [7:0] out_221,
  output [7:0] out_222,
  output [7:0] out_223,
  output [7:0] out_224,
  output [7:0] out_225,
  output [7:0] out_226,
  output [7:0] out_227,
  output [7:0] out_228,
  output [7:0] out_229,
  output [7:0] out_230,
  output [7:0] out_231,
  output [7:0] out_232,
  output [7:0] out_233,
  output [7:0] out_234,
  output [7:0] out_235,
  output [7:0] out_236,
  output [7:0] out_237,
  output [7:0] out_238,
  output [7:0] out_239,
  output [7:0] out_240,
  output [7:0] out_241,
  output [7:0] out_242,
  output [7:0] out_243,
  output [7:0] out_244,
  output [7:0] out_245,
  output [7:0] out_246,
  output [7:0] out_247,
  output [7:0] out_248,
  output [7:0] out_249,
  output [7:0] out_250,
  output [7:0] out_251,
  output [7:0] out_252,
  output [7:0] out_253,
  output [7:0] out_254,
  output [7:0] out_255,
  output [7:0] out_256,
  output [7:0] out_257,
  output [7:0] out_258,
  output [7:0] out_259,
  output [7:0] out_260,
  output [7:0] out_261,
  output [7:0] out_262,
  output [7:0] out_263,
  output [7:0] out_264,
  output [7:0] out_265,
  output [7:0] out_266
);

  wire H0, H1, H2, H3, H4, H5, H6, H7, H8, H9, H10, H11, H12, H13, H14, H15, V0, V1, V2, V3, V4, V5, V6, V7,
       V8, V9, V10, V11, V12, V13, V14, V15;
  wire [7:0] DOUT, mem_8_bits_1_out_3;

  assign RAM_OUT = in_5 ? DOUT : 8'bz;  // Controlled_Buffer controlled_buffer_1
  MEM_8_BITS mem_8_bits_1 (.s(in_2), .in_1(RAM_ADDR_IN), .out_3(mem_8_bits_1_out_3));
  CPU_DEC_4_16 cpu_dec_4_16_1 (
    .in_1(mem_8_bits_1_out_3[7:4]), .out_13(H11), .out_14(H12), .out_15(H13), .out_16(H14), .M(H15), .L(H0),
    .out_3(H1), .out_4(H2), .out_5(H3), .out_6(H4), .out_7(H5), .out_8(H6), .out_9(H7), .out_10(H8),
    .out_11(H9), .out_12(H10));
  MEM_BYTE mem_byte_1 (.h(H0), .v(V15), .s(in_4), .e(in_5), .r(in_6), .in_1(RAM_IN), .out_7(out_11), .out_8(DOUT));
  MEM_BYTE mem_byte_2 (.h(H1), .v(V15), .s(in_4), .e(in_5), .r(in_6), .in_1(RAM_IN), .out_7(out_27), .out_8(DOUT));
  MEM_BYTE mem_byte_3 (.h(H2), .v(V15), .s(in_4), .e(in_5), .r(in_6), .in_1(RAM_IN), .out_7(out_43), .out_8(DOUT));
  MEM_BYTE mem_byte_4 (.h(H3), .v(V15), .s(in_4), .e(in_5), .r(in_6), .in_1(RAM_IN), .out_7(out_59), .out_8(DOUT));
  MEM_BYTE mem_byte_5 (.h(H4), .v(V15), .s(in_4), .e(in_5), .r(in_6), .in_1(RAM_IN), .out_7(out_75), .out_8(DOUT));
  MEM_BYTE mem_byte_6 (.h(H5), .v(V15), .s(in_4), .e(in_5), .r(in_6), .in_1(RAM_IN), .out_7(out_91), .out_8(DOUT));
  MEM_BYTE mem_byte_7 (.h(H6), .v(V15), .s(in_4), .e(in_5), .r(in_6), .in_1(RAM_IN), .out_7(out_107), .out_8(DOUT));
  MEM_BYTE mem_byte_8 (.h(H7), .v(V15), .s(in_4), .e(in_5), .r(in_6), .in_1(RAM_IN), .out_7(out_123), .out_8(DOUT));
  MEM_BYTE mem_byte_9 (.h(H8), .v(V15), .s(in_4), .e(in_5), .r(in_6), .in_1(RAM_IN), .out_7(out_139), .out_8(DOUT));
  MEM_BYTE mem_byte_10 (.h(H9), .v(V15), .s(in_4), .e(in_5), .r(in_6), .in_1(RAM_IN), .out_7(out_155), .out_8(DOUT));
  MEM_BYTE mem_byte_11 (.h(H10), .v(V15), .s(in_4), .e(in_5), .r(in_6), .in_1(RAM_IN), .out_7(out_171), .out_8(DOUT));
  MEM_BYTE mem_byte_12 (.h(H11), .v(V15), .s(in_4), .e(in_5), .r(in_6), .in_1(RAM_IN), .out_7(out_187), .out_8(DOUT));
  MEM_BYTE mem_byte_13 (.h(H12), .v(V15), .s(in_4), .e(in_5), .r(in_6), .in_1(RAM_IN), .out_7(out_203), .out_8(DOUT));
  MEM_BYTE mem_byte_14 (.h(H13), .v(V15), .s(in_4), .e(in_5), .r(in_6), .in_1(RAM_IN), .out_7(out_219), .out_8(DOUT));
  MEM_BYTE mem_byte_15 (.h(H14), .v(V15), .s(in_4), .e(in_5), .r(in_6), .in_1(RAM_IN), .out_7(out_235), .out_8(DOUT));
  MEM_BYTE mem_byte_16 (.h(H15), .v(V15), .s(in_4), .e(in_5), .r(in_6), .in_1(RAM_IN), .out_7(out_251), .out_8(DOUT));
  MEM_BYTE mem_byte_17 (.h(H0), .v(V14), .s(in_4), .e(in_5), .r(in_6), .in_1(RAM_IN), .out_7(out_12), .out_8(DOUT));
  MEM_BYTE mem_byte_18 (.h(H1), .v(V14), .s(in_4), .e(in_5), .r(in_6), .in_1(RAM_IN), .out_7(out_28), .out_8(DOUT));
  MEM_BYTE mem_byte_19 (.h(H2), .v(V14), .s(in_4), .e(in_5), .r(in_6), .in_1(RAM_IN), .out_7(out_44), .out_8(DOUT));
  MEM_BYTE mem_byte_20 (.h(H3), .v(V14), .s(in_4), .e(in_5), .r(in_6), .in_1(RAM_IN), .out_7(out_60), .out_8(DOUT));
  MEM_BYTE mem_byte_21 (.h(H4), .v(V14), .s(in_4), .e(in_5), .r(in_6), .in_1(RAM_IN), .out_7(out_76), .out_8(DOUT));
  MEM_BYTE mem_byte_22 (.h(H5), .v(V14), .s(in_4), .e(in_5), .r(in_6), .in_1(RAM_IN), .out_7(out_92), .out_8(DOUT));
  MEM_BYTE mem_byte_23 (.h(H6), .v(V14), .s(in_4), .e(in_5), .r(in_6), .in_1(RAM_IN), .out_7(out_108), .out_8(DOUT));
  MEM_BYTE mem_byte_24 (.h(H7), .v(V14), .s(in_4), .e(in_5), .r(in_6), .in_1(RAM_IN), .out_7(out_124), .out_8(DOUT));
  MEM_BYTE mem_byte_25 (.h(H8), .v(V14), .s(in_4), .e(in_5), .r(in_6), .in_1(RAM_IN), .out_7(out_140), .out_8(DOUT));
  MEM_BYTE mem_byte_26 (.h(H9), .v(V14), .s(in_4), .e(in_5), .r(in_6), .in_1(RAM_IN), .out_7(out_156), .out_8(DOUT));
  MEM_BYTE mem_byte_27 (.h(H10), .v(V14), .s(in_4), .e(in_5), .r(in_6), .in_1(RAM_IN), .out_7(out_172), .out_8(DOUT));
  MEM_BYTE mem_byte_28 (.h(H11), .v(V14), .s(in_4), .e(in_5), .r(in_6), .in_1(RAM_IN), .out_7(out_188), .out_8(DOUT));
  MEM_BYTE mem_byte_29 (.h(H12), .v(V14), .s(in_4), .e(in_5), .r(in_6), .in_1(RAM_IN), .out_7(out_204), .out_8(DOUT));
  MEM_BYTE mem_byte_30 (.h(H13), .v(V14), .s(in_4), .e(in_5), .r(in_6), .in_1(RAM_IN), .out_7(out_220), .out_8(DOUT));
  MEM_BYTE mem_byte_31 (.h(H14), .v(V14), .s(in_4), .e(in_5), .r(in_6), .in_1(RAM_IN), .out_7(out_236), .out_8(DOUT));
  MEM_BYTE mem_byte_32 (.h(H15), .v(V14), .s(in_4), .e(in_5), .r(in_6), .in_1(RAM_IN), .out_7(out_252), .out_8(DOUT));
  CPU_DEC_4_16 cpu_dec_4_16_2 (
    .in_1(mem_8_bits_1_out_3[3:0]), .out_13(V11), .out_14(V12), .out_15(V13), .out_16(V14), .M(V15), .L(V0),
    .out_3(V1), .out_4(V2), .out_5(V3), .out_6(V4), .out_7(V5), .out_8(V6), .out_9(V7), .out_10(V8),
    .out_11(V9), .out_12(V10));
  MEM_BYTE mem_byte_33 (.h(H0), .v(V13), .s(in_4), .e(in_5), .r(in_6), .in_1(RAM_IN), .out_7(out_13), .out_8(DOUT));
  MEM_BYTE mem_byte_34 (.h(H1), .v(V13), .s(in_4), .e(in_5), .r(in_6), .in_1(RAM_IN), .out_7(out_29), .out_8(DOUT));
  MEM_BYTE mem_byte_35 (.h(H2), .v(V13), .s(in_4), .e(in_5), .r(in_6), .in_1(RAM_IN), .out_7(out_45), .out_8(DOUT));
  MEM_BYTE mem_byte_36 (.h(H3), .v(V13), .s(in_4), .e(in_5), .r(in_6), .in_1(RAM_IN), .out_7(out_61), .out_8(DOUT));
  MEM_BYTE mem_byte_37 (.h(H4), .v(V13), .s(in_4), .e(in_5), .r(in_6), .in_1(RAM_IN), .out_7(out_77), .out_8(DOUT));
  MEM_BYTE mem_byte_38 (.h(H5), .v(V13), .s(in_4), .e(in_5), .r(in_6), .in_1(RAM_IN), .out_7(out_93), .out_8(DOUT));
  MEM_BYTE mem_byte_39 (.h(H6), .v(V13), .s(in_4), .e(in_5), .r(in_6), .in_1(RAM_IN), .out_7(out_109), .out_8(DOUT));
  MEM_BYTE mem_byte_40 (.h(H7), .v(V13), .s(in_4), .e(in_5), .r(in_6), .in_1(RAM_IN), .out_7(out_125), .out_8(DOUT));
  MEM_BYTE mem_byte_41 (.h(H8), .v(V13), .s(in_4), .e(in_5), .r(in_6), .in_1(RAM_IN), .out_7(out_141), .out_8(DOUT));
  MEM_BYTE mem_byte_42 (.h(H9), .v(V13), .s(in_4), .e(in_5), .r(in_6), .in_1(RAM_IN), .out_7(out_157), .out_8(DOUT));
  MEM_BYTE mem_byte_43 (.h(H10), .v(V13), .s(in_4), .e(in_5), .r(in_6), .in_1(RAM_IN), .out_7(out_173), .out_8(DOUT));
  MEM_BYTE mem_byte_44 (.h(H11), .v(V13), .s(in_4), .e(in_5), .r(in_6), .in_1(RAM_IN), .out_7(out_189), .out_8(DOUT));
  MEM_BYTE mem_byte_45 (.h(H12), .v(V13), .s(in_4), .e(in_5), .r(in_6), .in_1(RAM_IN), .out_7(out_205), .out_8(DOUT));
  MEM_BYTE mem_byte_46 (.h(H13), .v(V13), .s(in_4), .e(in_5), .r(in_6), .in_1(RAM_IN), .out_7(out_221), .out_8(DOUT));
  MEM_BYTE mem_byte_47 (.h(H14), .v(V13), .s(in_4), .e(in_5), .r(in_6), .in_1(RAM_IN), .out_7(out_237), .out_8(DOUT));
  MEM_BYTE mem_byte_48 (.h(H15), .v(V13), .s(in_4), .e(in_5), .r(in_6), .in_1(RAM_IN), .out_7(out_253), .out_8(DOUT));
  MEM_BYTE mem_byte_49 (.h(H0), .v(V12), .s(in_4), .e(in_5), .r(in_6), .in_1(RAM_IN), .out_7(out_14), .out_8(DOUT));
  MEM_BYTE mem_byte_50 (.h(H1), .v(V12), .s(in_4), .e(in_5), .r(in_6), .in_1(RAM_IN), .out_7(out_30), .out_8(DOUT));
  MEM_BYTE mem_byte_51 (.h(H2), .v(V12), .s(in_4), .e(in_5), .r(in_6), .in_1(RAM_IN), .out_7(out_46), .out_8(DOUT));
  MEM_BYTE mem_byte_52 (.h(H3), .v(V12), .s(in_4), .e(in_5), .r(in_6), .in_1(RAM_IN), .out_7(out_62), .out_8(DOUT));
  MEM_BYTE mem_byte_53 (.h(H4), .v(V12), .s(in_4), .e(in_5), .r(in_6), .in_1(RAM_IN), .out_7(out_78), .out_8(DOUT));
  MEM_BYTE mem_byte_54 (.h(H5), .v(V12), .s(in_4), .e(in_5), .r(in_6), .in_1(RAM_IN), .out_7(out_94), .out_8(DOUT));
  MEM_BYTE mem_byte_55 (.h(H6), .v(V12), .s(in_4), .e(in_5), .r(in_6), .in_1(RAM_IN), .out_7(out_110), .out_8(DOUT));
  MEM_BYTE mem_byte_56 (.h(H7), .v(V12), .s(in_4), .e(in_5), .r(in_6), .in_1(RAM_IN), .out_7(out_126), .out_8(DOUT));
  MEM_BYTE mem_byte_57 (.h(H8), .v(V12), .s(in_4), .e(in_5), .r(in_6), .in_1(RAM_IN), .out_7(out_142), .out_8(DOUT));
  MEM_BYTE mem_byte_58 (.h(H9), .v(V12), .s(in_4), .e(in_5), .r(in_6), .in_1(RAM_IN), .out_7(out_158), .out_8(DOUT));
  MEM_BYTE mem_byte_59 (.h(H10), .v(V12), .s(in_4), .e(in_5), .r(in_6), .in_1(RAM_IN), .out_7(out_174), .out_8(DOUT));
  MEM_BYTE mem_byte_60 (.h(H11), .v(V12), .s(in_4), .e(in_5), .r(in_6), .in_1(RAM_IN), .out_7(out_190), .out_8(DOUT));
  MEM_BYTE mem_byte_61 (.h(H12), .v(V12), .s(in_4), .e(in_5), .r(in_6), .in_1(RAM_IN), .out_7(out_206), .out_8(DOUT));
  MEM_BYTE mem_byte_62 (.h(H13), .v(V12), .s(in_4), .e(in_5), .r(in_6), .in_1(RAM_IN), .out_7(out_222), .out_8(DOUT));
  MEM_BYTE mem_byte_63 (.h(H14), .v(V12), .s(in_4), .e(in_5), .r(in_6), .in_1(RAM_IN), .out_7(out_238), .out_8(DOUT));
  MEM_BYTE mem_byte_64 (.h(H15), .v(V12), .s(in_4), .e(in_5), .r(in_6), .in_1(RAM_IN), .out_7(out_254), .out_8(DOUT));
  MEM_BYTE mem_byte_65 (.h(H0), .v(V11), .s(in_4), .e(in_5), .r(in_6), .in_1(RAM_IN), .out_7(out_15), .out_8(DOUT));
  MEM_BYTE mem_byte_66 (.h(H1), .v(V11), .s(in_4), .e(in_5), .r(in_6), .in_1(RAM_IN), .out_7(out_31), .out_8(DOUT));
  MEM_BYTE mem_byte_67 (.h(H2), .v(V11), .s(in_4), .e(in_5), .r(in_6), .in_1(RAM_IN), .out_7(out_47), .out_8(DOUT));
  MEM_BYTE mem_byte_68 (.h(H3), .v(V11), .s(in_4), .e(in_5), .r(in_6), .in_1(RAM_IN), .out_7(out_63), .out_8(DOUT));
  MEM_BYTE mem_byte_69 (.h(H4), .v(V11), .s(in_4), .e(in_5), .r(in_6), .in_1(RAM_IN), .out_7(out_79), .out_8(DOUT));
  MEM_BYTE mem_byte_70 (.h(H5), .v(V11), .s(in_4), .e(in_5), .r(in_6), .in_1(RAM_IN), .out_7(out_95), .out_8(DOUT));
  MEM_BYTE mem_byte_71 (.h(H6), .v(V11), .s(in_4), .e(in_5), .r(in_6), .in_1(RAM_IN), .out_7(out_111), .out_8(DOUT));
  MEM_BYTE mem_byte_72 (.h(H7), .v(V11), .s(in_4), .e(in_5), .r(in_6), .in_1(RAM_IN), .out_7(out_127), .out_8(DOUT));
  MEM_BYTE mem_byte_73 (.h(H8), .v(V11), .s(in_4), .e(in_5), .r(in_6), .in_1(RAM_IN), .out_7(out_143), .out_8(DOUT));
  MEM_BYTE mem_byte_74 (.h(H9), .v(V11), .s(in_4), .e(in_5), .r(in_6), .in_1(RAM_IN), .out_7(out_159), .out_8(DOUT));
  MEM_BYTE mem_byte_75 (.h(H10), .v(V11), .s(in_4), .e(in_5), .r(in_6), .in_1(RAM_IN), .out_7(out_175), .out_8(DOUT));
  MEM_BYTE mem_byte_76 (.h(H11), .v(V11), .s(in_4), .e(in_5), .r(in_6), .in_1(RAM_IN), .out_7(out_191), .out_8(DOUT));
  MEM_BYTE mem_byte_77 (.h(H12), .v(V11), .s(in_4), .e(in_5), .r(in_6), .in_1(RAM_IN), .out_7(out_207), .out_8(DOUT));
  MEM_BYTE mem_byte_78 (.h(H13), .v(V11), .s(in_4), .e(in_5), .r(in_6), .in_1(RAM_IN), .out_7(out_223), .out_8(DOUT));
  MEM_BYTE mem_byte_79 (.h(H14), .v(V11), .s(in_4), .e(in_5), .r(in_6), .in_1(RAM_IN), .out_7(out_239), .out_8(DOUT));
  MEM_BYTE mem_byte_80 (.h(H15), .v(V11), .s(in_4), .e(in_5), .r(in_6), .in_1(RAM_IN), .out_7(out_255), .out_8(DOUT));
  MEM_BYTE mem_byte_81 (.h(H0), .v(V10), .s(in_4), .e(in_5), .r(in_6), .in_1(RAM_IN), .out_7(out_16), .out_8(DOUT));
  MEM_BYTE mem_byte_82 (.h(H1), .v(V10), .s(in_4), .e(in_5), .r(in_6), .in_1(RAM_IN), .out_7(out_32), .out_8(DOUT));
  MEM_BYTE mem_byte_83 (.h(H2), .v(V10), .s(in_4), .e(in_5), .r(in_6), .in_1(RAM_IN), .out_7(out_48), .out_8(DOUT));
  MEM_BYTE mem_byte_84 (.h(H3), .v(V10), .s(in_4), .e(in_5), .r(in_6), .in_1(RAM_IN), .out_7(out_64), .out_8(DOUT));
  MEM_BYTE mem_byte_85 (.h(H4), .v(V10), .s(in_4), .e(in_5), .r(in_6), .in_1(RAM_IN), .out_7(out_80), .out_8(DOUT));
  MEM_BYTE mem_byte_86 (.h(H5), .v(V10), .s(in_4), .e(in_5), .r(in_6), .in_1(RAM_IN), .out_7(out_96), .out_8(DOUT));
  MEM_BYTE mem_byte_87 (.h(H6), .v(V10), .s(in_4), .e(in_5), .r(in_6), .in_1(RAM_IN), .out_7(out_112), .out_8(DOUT));
  MEM_BYTE mem_byte_88 (.h(H7), .v(V10), .s(in_4), .e(in_5), .r(in_6), .in_1(RAM_IN), .out_7(out_128), .out_8(DOUT));
  MEM_BYTE mem_byte_89 (.h(H8), .v(V10), .s(in_4), .e(in_5), .r(in_6), .in_1(RAM_IN), .out_7(out_144), .out_8(DOUT));
  MEM_BYTE mem_byte_90 (.h(H9), .v(V10), .s(in_4), .e(in_5), .r(in_6), .in_1(RAM_IN), .out_7(out_160), .out_8(DOUT));
  MEM_BYTE mem_byte_91 (.h(H10), .v(V10), .s(in_4), .e(in_5), .r(in_6), .in_1(RAM_IN), .out_7(out_176), .out_8(DOUT));
  MEM_BYTE mem_byte_92 (.h(H11), .v(V10), .s(in_4), .e(in_5), .r(in_6), .in_1(RAM_IN), .out_7(out_192), .out_8(DOUT));
  MEM_BYTE mem_byte_93 (.h(H12), .v(V10), .s(in_4), .e(in_5), .r(in_6), .in_1(RAM_IN), .out_7(out_208), .out_8(DOUT));
  MEM_BYTE mem_byte_94 (.h(H13), .v(V10), .s(in_4), .e(in_5), .r(in_6), .in_1(RAM_IN), .out_7(out_224), .out_8(DOUT));
  MEM_BYTE mem_byte_95 (.h(H14), .v(V10), .s(in_4), .e(in_5), .r(in_6), .in_1(RAM_IN), .out_7(out_240), .out_8(DOUT));
  MEM_BYTE mem_byte_96 (.h(H15), .v(V0), .s(in_4), .e(in_5), .r(in_6), .in_1(RAM_IN), .out_7(out_256), .out_8(DOUT));
  MEM_BYTE mem_byte_97 (.h(H0), .v(V9), .s(in_4), .e(in_5), .r(in_6), .in_1(RAM_IN), .out_7(out_17), .out_8(DOUT));
  MEM_BYTE mem_byte_98 (.h(H1), .v(V9), .s(in_4), .e(in_5), .r(in_6), .in_1(RAM_IN), .out_7(out_33), .out_8(DOUT));
  MEM_BYTE mem_byte_99 (.h(H2), .v(V9), .s(in_4), .e(in_5), .r(in_6), .in_1(RAM_IN), .out_7(out_49), .out_8(DOUT));
  MEM_BYTE mem_byte_100 (.h(H3), .v(V9), .s(in_4), .e(in_5), .r(in_6), .in_1(RAM_IN), .out_7(out_65), .out_8(DOUT));
  MEM_BYTE mem_byte_101 (.h(H4), .v(V9), .s(in_4), .e(in_5), .r(in_6), .in_1(RAM_IN), .out_7(out_81), .out_8(DOUT));
  MEM_BYTE mem_byte_102 (.h(H5), .v(V9), .s(in_4), .e(in_5), .r(in_6), .in_1(RAM_IN), .out_7(out_97), .out_8(DOUT));
  MEM_BYTE mem_byte_103 (.h(H6), .v(V9), .s(in_4), .e(in_5), .r(in_6), .in_1(RAM_IN), .out_7(out_113), .out_8(DOUT));
  MEM_BYTE mem_byte_104 (.h(H7), .v(V9), .s(in_4), .e(in_5), .r(in_6), .in_1(RAM_IN), .out_7(out_129), .out_8(DOUT));
  MEM_BYTE mem_byte_105 (.h(H8), .v(V9), .s(in_4), .e(in_5), .r(in_6), .in_1(RAM_IN), .out_7(out_145), .out_8(DOUT));
  MEM_BYTE mem_byte_106 (.h(H9), .v(V9), .s(in_4), .e(in_5), .r(in_6), .in_1(RAM_IN), .out_7(out_161), .out_8(DOUT));
  MEM_BYTE mem_byte_107 (.h(H10), .v(V9), .s(in_4), .e(in_5), .r(in_6), .in_1(RAM_IN), .out_7(out_177), .out_8(DOUT));
  MEM_BYTE mem_byte_108 (.h(H11), .v(V9), .s(in_4), .e(in_5), .r(in_6), .in_1(RAM_IN), .out_7(out_193), .out_8(DOUT));
  MEM_BYTE mem_byte_109 (.h(H12), .v(V9), .s(in_4), .e(in_5), .r(in_6), .in_1(RAM_IN), .out_7(out_209), .out_8(DOUT));
  MEM_BYTE mem_byte_110 (.h(H13), .v(V9), .s(in_4), .e(in_5), .r(in_6), .in_1(RAM_IN), .out_7(out_225), .out_8(DOUT));
  MEM_BYTE mem_byte_111 (.h(H14), .v(V9), .s(in_4), .e(in_5), .r(in_6), .in_1(RAM_IN), .out_7(out_241), .out_8(DOUT));
  MEM_BYTE mem_byte_112 (.h(H15), .v(V9), .s(in_4), .e(in_5), .r(in_6), .in_1(RAM_IN), .out_7(out_257), .out_8(DOUT));
  MEM_BYTE mem_byte_113 (.h(H0), .v(V8), .s(in_4), .e(in_5), .r(in_6), .in_1(RAM_IN), .out_7(out_18), .out_8(DOUT));
  MEM_BYTE mem_byte_114 (.h(H1), .v(V8), .s(in_4), .e(in_5), .r(in_6), .in_1(RAM_IN), .out_7(out_34), .out_8(DOUT));
  MEM_BYTE mem_byte_115 (.h(H2), .v(V8), .s(in_4), .e(in_5), .r(in_6), .in_1(RAM_IN), .out_7(out_50), .out_8(DOUT));
  MEM_BYTE mem_byte_116 (.h(H3), .v(V8), .s(in_4), .e(in_5), .r(in_6), .in_1(RAM_IN), .out_7(out_66), .out_8(DOUT));
  MEM_BYTE mem_byte_117 (.h(H4), .v(V8), .s(in_4), .e(in_5), .r(in_6), .in_1(RAM_IN), .out_7(out_82), .out_8(DOUT));
  MEM_BYTE mem_byte_118 (.h(H5), .v(V8), .s(in_4), .e(in_5), .r(in_6), .in_1(RAM_IN), .out_7(out_98), .out_8(DOUT));
  MEM_BYTE mem_byte_119 (.h(H6), .v(V8), .s(in_4), .e(in_5), .r(in_6), .in_1(RAM_IN), .out_7(out_114), .out_8(DOUT));
  MEM_BYTE mem_byte_120 (.h(H7), .v(V8), .s(in_4), .e(in_5), .r(in_6), .in_1(RAM_IN), .out_7(out_130), .out_8(DOUT));
  MEM_BYTE mem_byte_121 (.h(H8), .v(V8), .s(in_4), .e(in_5), .r(in_6), .in_1(RAM_IN), .out_7(out_146), .out_8(DOUT));
  MEM_BYTE mem_byte_122 (.h(H9), .v(V8), .s(in_4), .e(in_5), .r(in_6), .in_1(RAM_IN), .out_7(out_162), .out_8(DOUT));
  MEM_BYTE mem_byte_123 (.h(H10), .v(V8), .s(in_4), .e(in_5), .r(in_6), .in_1(RAM_IN), .out_7(out_178), .out_8(DOUT));
  MEM_BYTE mem_byte_124 (.h(H11), .v(V8), .s(in_4), .e(in_5), .r(in_6), .in_1(RAM_IN), .out_7(out_194), .out_8(DOUT));
  MEM_BYTE mem_byte_125 (.h(H12), .v(V8), .s(in_4), .e(in_5), .r(in_6), .in_1(RAM_IN), .out_7(out_210), .out_8(DOUT));
  MEM_BYTE mem_byte_126 (.h(H13), .v(V8), .s(in_4), .e(in_5), .r(in_6), .in_1(RAM_IN), .out_7(out_226), .out_8(DOUT));
  MEM_BYTE mem_byte_127 (.h(H14), .v(V8), .s(in_4), .e(in_5), .r(in_6), .in_1(RAM_IN), .out_7(out_242), .out_8(DOUT));
  MEM_BYTE mem_byte_128 (.h(H15), .v(V8), .s(in_4), .e(in_5), .r(in_6), .in_1(RAM_IN), .out_7(out_258), .out_8(DOUT));
  MEM_BYTE mem_byte_129 (.h(H0), .v(V7), .s(in_4), .e(in_5), .r(in_6), .in_1(RAM_IN), .out_7(out_19), .out_8(DOUT));
  MEM_BYTE mem_byte_130 (.h(H1), .v(V7), .s(in_4), .e(in_5), .r(in_6), .in_1(RAM_IN), .out_7(out_35), .out_8(DOUT));
  MEM_BYTE mem_byte_131 (.h(H2), .v(V7), .s(in_4), .e(in_5), .r(in_6), .in_1(RAM_IN), .out_7(out_51), .out_8(DOUT));
  MEM_BYTE mem_byte_132 (.h(H3), .v(V7), .s(in_4), .e(in_5), .r(in_6), .in_1(RAM_IN), .out_7(out_67), .out_8(DOUT));
  MEM_BYTE mem_byte_133 (.h(H4), .v(V7), .s(in_4), .e(in_5), .r(in_6), .in_1(RAM_IN), .out_7(out_83), .out_8(DOUT));
  MEM_BYTE mem_byte_134 (.h(H5), .v(V7), .s(in_4), .e(in_5), .r(in_6), .in_1(RAM_IN), .out_7(out_99), .out_8(DOUT));
  MEM_BYTE mem_byte_135 (.h(H6), .v(V7), .s(in_4), .e(in_5), .r(in_6), .in_1(RAM_IN), .out_7(out_115), .out_8(DOUT));
  MEM_BYTE mem_byte_136 (.h(H7), .v(V7), .s(in_4), .e(in_5), .r(in_6), .in_1(RAM_IN), .out_7(out_131), .out_8(DOUT));
  MEM_BYTE mem_byte_137 (.h(H8), .v(V7), .s(in_4), .e(in_5), .r(in_6), .in_1(RAM_IN), .out_7(out_147), .out_8(DOUT));
  MEM_BYTE mem_byte_138 (.h(H9), .v(V7), .s(in_4), .e(in_5), .r(in_6), .in_1(RAM_IN), .out_7(out_163), .out_8(DOUT));
  MEM_BYTE mem_byte_139 (.h(H10), .v(V7), .s(in_4), .e(in_5), .r(in_6), .in_1(RAM_IN), .out_7(out_179), .out_8(DOUT));
  MEM_BYTE mem_byte_140 (.h(H11), .v(V7), .s(in_4), .e(in_5), .r(in_6), .in_1(RAM_IN), .out_7(out_195), .out_8(DOUT));
  MEM_BYTE mem_byte_141 (.h(H12), .v(V7), .s(in_4), .e(in_5), .r(in_6), .in_1(RAM_IN), .out_7(out_211), .out_8(DOUT));
  MEM_BYTE mem_byte_142 (.h(H13), .v(V7), .s(in_4), .e(in_5), .r(in_6), .in_1(RAM_IN), .out_7(out_227), .out_8(DOUT));
  MEM_BYTE mem_byte_143 (.h(H14), .v(V7), .s(in_4), .e(in_5), .r(in_6), .in_1(RAM_IN), .out_7(out_243), .out_8(DOUT));
  MEM_BYTE mem_byte_144 (.h(H15), .v(V7), .s(in_4), .e(in_5), .r(in_6), .in_1(RAM_IN), .out_7(out_259), .out_8(DOUT));
  MEM_BYTE mem_byte_145 (.h(H0), .v(V6), .s(in_4), .e(in_5), .r(in_6), .in_1(RAM_IN), .out_7(out_20), .out_8(DOUT));
  MEM_BYTE mem_byte_146 (.h(H1), .v(V6), .s(in_4), .e(in_5), .r(in_6), .in_1(RAM_IN), .out_7(out_36), .out_8(DOUT));
  MEM_BYTE mem_byte_147 (.h(H2), .v(V6), .s(in_4), .e(in_5), .r(in_6), .in_1(RAM_IN), .out_7(out_52), .out_8(DOUT));
  MEM_BYTE mem_byte_148 (.h(H3), .v(V6), .s(in_4), .e(in_5), .r(in_6), .in_1(RAM_IN), .out_7(out_68), .out_8(DOUT));
  MEM_BYTE mem_byte_149 (.h(H4), .v(V6), .s(in_4), .e(in_5), .r(in_6), .in_1(RAM_IN), .out_7(out_84), .out_8(DOUT));
  MEM_BYTE mem_byte_150 (.h(H5), .v(V6), .s(in_4), .e(in_5), .r(in_6), .in_1(RAM_IN), .out_7(out_100), .out_8(DOUT));
  MEM_BYTE mem_byte_151 (.h(H6), .v(V6), .s(in_4), .e(in_5), .r(in_6), .in_1(RAM_IN), .out_7(out_116), .out_8(DOUT));
  MEM_BYTE mem_byte_152 (.h(H7), .v(V6), .s(in_4), .e(in_5), .r(in_6), .in_1(RAM_IN), .out_7(out_132), .out_8(DOUT));
  MEM_BYTE mem_byte_153 (.h(H8), .v(V6), .s(in_4), .e(in_5), .r(in_6), .in_1(RAM_IN), .out_7(out_148), .out_8(DOUT));
  MEM_BYTE mem_byte_154 (.h(H9), .v(V6), .s(in_4), .e(in_5), .r(in_6), .in_1(RAM_IN), .out_7(out_164), .out_8(DOUT));
  MEM_BYTE mem_byte_155 (.h(H10), .v(V6), .s(in_4), .e(in_5), .r(in_6), .in_1(RAM_IN), .out_7(out_180), .out_8(DOUT));
  MEM_BYTE mem_byte_156 (.h(H11), .v(V6), .s(in_4), .e(in_5), .r(in_6), .in_1(RAM_IN), .out_7(out_196), .out_8(DOUT));
  MEM_BYTE mem_byte_157 (.h(H12), .v(V6), .s(in_4), .e(in_5), .r(in_6), .in_1(RAM_IN), .out_7(out_212), .out_8(DOUT));
  MEM_BYTE mem_byte_158 (.h(H13), .v(V6), .s(in_4), .e(in_5), .r(in_6), .in_1(RAM_IN), .out_7(out_228), .out_8(DOUT));
  MEM_BYTE mem_byte_159 (.h(H14), .v(V6), .s(in_4), .e(in_5), .r(in_6), .in_1(RAM_IN), .out_7(out_244), .out_8(DOUT));
  MEM_BYTE mem_byte_160 (.h(H15), .v(V6), .s(in_4), .e(in_5), .r(in_6), .in_1(RAM_IN), .out_7(out_260), .out_8(DOUT));
  MEM_BYTE mem_byte_161 (.h(H0), .v(V5), .s(in_4), .e(in_5), .r(in_6), .in_1(RAM_IN), .out_7(out_21), .out_8(DOUT));
  MEM_BYTE mem_byte_162 (.h(H1), .v(V5), .s(in_4), .e(in_5), .r(in_6), .in_1(RAM_IN), .out_7(out_37), .out_8(DOUT));
  MEM_BYTE mem_byte_163 (.h(H2), .v(V5), .s(in_4), .e(in_5), .r(in_6), .in_1(RAM_IN), .out_7(out_53), .out_8(DOUT));
  MEM_BYTE mem_byte_164 (.h(H3), .v(V5), .s(in_4), .e(in_5), .r(in_6), .in_1(RAM_IN), .out_7(out_69), .out_8(DOUT));
  MEM_BYTE mem_byte_165 (.h(H4), .v(V5), .s(in_4), .e(in_5), .r(in_6), .in_1(RAM_IN), .out_7(out_85), .out_8(DOUT));
  MEM_BYTE mem_byte_166 (.h(H5), .v(V5), .s(in_4), .e(in_5), .r(in_6), .in_1(RAM_IN), .out_7(out_101), .out_8(DOUT));
  MEM_BYTE mem_byte_167 (.h(H6), .v(V5), .s(in_4), .e(in_5), .r(in_6), .in_1(RAM_IN), .out_7(out_117), .out_8(DOUT));
  MEM_BYTE mem_byte_168 (.h(H7), .v(V5), .s(in_4), .e(in_5), .r(in_6), .in_1(RAM_IN), .out_7(out_133), .out_8(DOUT));
  MEM_BYTE mem_byte_169 (.h(H8), .v(V5), .s(in_4), .e(in_5), .r(in_6), .in_1(RAM_IN), .out_7(out_149), .out_8(DOUT));
  MEM_BYTE mem_byte_170 (.h(H9), .v(V5), .s(in_4), .e(in_5), .r(in_6), .in_1(RAM_IN), .out_7(out_165), .out_8(DOUT));
  MEM_BYTE mem_byte_171 (.h(H10), .v(V5), .s(in_4), .e(in_5), .r(in_6), .in_1(RAM_IN), .out_7(out_181), .out_8(DOUT));
  MEM_BYTE mem_byte_172 (.h(H11), .v(V5), .s(in_4), .e(in_5), .r(in_6), .in_1(RAM_IN), .out_7(out_197), .out_8(DOUT));
  MEM_BYTE mem_byte_173 (.h(H12), .v(V5), .s(in_4), .e(in_5), .r(in_6), .in_1(RAM_IN), .out_7(out_213), .out_8(DOUT));
  MEM_BYTE mem_byte_174 (.h(H13), .v(V5), .s(in_4), .e(in_5), .r(in_6), .in_1(RAM_IN), .out_7(out_229), .out_8(DOUT));
  MEM_BYTE mem_byte_175 (.h(H14), .v(V5), .s(in_4), .e(in_5), .r(in_6), .in_1(RAM_IN), .out_7(out_245), .out_8(DOUT));
  MEM_BYTE mem_byte_176 (.h(H15), .v(V5), .s(in_4), .e(in_5), .r(in_6), .in_1(RAM_IN), .out_7(out_261), .out_8(DOUT));
  MEM_BYTE mem_byte_177 (.h(H0), .v(V4), .s(in_4), .e(in_5), .r(in_6), .in_1(RAM_IN), .out_7(out_22), .out_8(DOUT));
  MEM_BYTE mem_byte_178 (.h(H1), .v(V4), .s(in_4), .e(in_5), .r(in_6), .in_1(RAM_IN), .out_7(out_38), .out_8(DOUT));
  MEM_BYTE mem_byte_179 (.h(H2), .v(V4), .s(in_4), .e(in_5), .r(in_6), .in_1(RAM_IN), .out_7(out_54), .out_8(DOUT));
  MEM_BYTE mem_byte_180 (.h(H3), .v(V4), .s(in_4), .e(in_5), .r(in_6), .in_1(RAM_IN), .out_7(out_70), .out_8(DOUT));
  MEM_BYTE mem_byte_181 (.h(H4), .v(V4), .s(in_4), .e(in_5), .r(in_6), .in_1(RAM_IN), .out_7(out_86), .out_8(DOUT));
  MEM_BYTE mem_byte_182 (.h(H5), .v(V4), .s(in_4), .e(in_5), .r(in_6), .in_1(RAM_IN), .out_7(out_102), .out_8(DOUT));
  MEM_BYTE mem_byte_183 (.h(H6), .v(V4), .s(in_4), .e(in_5), .r(in_6), .in_1(RAM_IN), .out_7(out_118), .out_8(DOUT));
  MEM_BYTE mem_byte_184 (.h(H7), .v(V4), .s(in_4), .e(in_5), .r(in_6), .in_1(RAM_IN), .out_7(out_134), .out_8(DOUT));
  MEM_BYTE mem_byte_185 (.h(H8), .v(V4), .s(in_4), .e(in_5), .r(in_6), .in_1(RAM_IN), .out_7(out_150), .out_8(DOUT));
  MEM_BYTE mem_byte_186 (.h(H9), .v(V4), .s(in_4), .e(in_5), .r(in_6), .in_1(RAM_IN), .out_7(out_166), .out_8(DOUT));
  MEM_BYTE mem_byte_187 (.h(H10), .v(V4), .s(in_4), .e(in_5), .r(in_6), .in_1(RAM_IN), .out_7(out_182), .out_8(DOUT));
  MEM_BYTE mem_byte_188 (.h(H11), .v(V4), .s(in_4), .e(in_5), .r(in_6), .in_1(RAM_IN), .out_7(out_198), .out_8(DOUT));
  MEM_BYTE mem_byte_189 (.h(H12), .v(V4), .s(in_4), .e(in_5), .r(in_6), .in_1(RAM_IN), .out_7(out_214), .out_8(DOUT));
  MEM_BYTE mem_byte_190 (.h(H13), .v(V4), .s(in_4), .e(in_5), .r(in_6), .in_1(RAM_IN), .out_7(out_230), .out_8(DOUT));
  MEM_BYTE mem_byte_191 (.h(H14), .v(V4), .s(in_4), .e(in_5), .r(in_6), .in_1(RAM_IN), .out_7(out_246), .out_8(DOUT));
  MEM_BYTE mem_byte_192 (.h(H15), .v(V4), .s(in_4), .e(in_5), .r(in_6), .in_1(RAM_IN), .out_7(out_262), .out_8(DOUT));
  MEM_BYTE mem_byte_193 (.h(H0), .v(V3), .s(in_4), .e(in_5), .r(in_6), .in_1(RAM_IN), .out_7(out_23), .out_8(DOUT));
  MEM_BYTE mem_byte_194 (.h(H1), .v(V3), .s(in_4), .e(in_5), .r(in_6), .in_1(RAM_IN), .out_7(out_39), .out_8(DOUT));
  MEM_BYTE mem_byte_195 (.h(H2), .v(V3), .s(in_4), .e(in_5), .r(in_6), .in_1(RAM_IN), .out_7(out_55), .out_8(DOUT));
  MEM_BYTE mem_byte_196 (.h(H3), .v(V3), .s(in_4), .e(in_5), .r(in_6), .in_1(RAM_IN), .out_7(out_71), .out_8(DOUT));
  MEM_BYTE mem_byte_197 (.h(H4), .v(V3), .s(in_4), .e(in_5), .r(in_6), .in_1(RAM_IN), .out_7(out_87), .out_8(DOUT));
  MEM_BYTE mem_byte_198 (.h(H5), .v(V3), .s(in_4), .e(in_5), .r(in_6), .in_1(RAM_IN), .out_7(out_103), .out_8(DOUT));
  MEM_BYTE mem_byte_199 (.h(H6), .v(V3), .s(in_4), .e(in_5), .r(in_6), .in_1(RAM_IN), .out_7(out_119), .out_8(DOUT));
  MEM_BYTE mem_byte_200 (.h(H7), .v(V3), .s(in_4), .e(in_5), .r(in_6), .in_1(RAM_IN), .out_7(out_135), .out_8(DOUT));
  MEM_BYTE mem_byte_201 (.h(H8), .v(V3), .s(in_4), .e(in_5), .r(in_6), .in_1(RAM_IN), .out_7(out_151), .out_8(DOUT));
  MEM_BYTE mem_byte_202 (.h(H9), .v(V3), .s(in_4), .e(in_5), .r(in_6), .in_1(RAM_IN), .out_7(out_167), .out_8(DOUT));
  MEM_BYTE mem_byte_203 (.h(H10), .v(V3), .s(in_4), .e(in_5), .r(in_6), .in_1(RAM_IN), .out_7(out_183), .out_8(DOUT));
  MEM_BYTE mem_byte_204 (.h(H11), .v(V3), .s(in_4), .e(in_5), .r(in_6), .in_1(RAM_IN), .out_7(out_199), .out_8(DOUT));
  MEM_BYTE mem_byte_205 (.h(H12), .v(V3), .s(in_4), .e(in_5), .r(in_6), .in_1(RAM_IN), .out_7(out_215), .out_8(DOUT));
  MEM_BYTE mem_byte_206 (.h(H13), .v(V3), .s(in_4), .e(in_5), .r(in_6), .in_1(RAM_IN), .out_7(out_231), .out_8(DOUT));
  MEM_BYTE mem_byte_207 (.h(H14), .v(V3), .s(in_4), .e(in_5), .r(in_6), .in_1(RAM_IN), .out_7(out_247), .out_8(DOUT));
  MEM_BYTE mem_byte_208 (.h(H15), .v(V3), .s(in_4), .e(in_5), .r(in_6), .in_1(RAM_IN), .out_7(out_263), .out_8(DOUT));
  MEM_BYTE mem_byte_209 (.h(H0), .v(V2), .s(in_4), .e(in_5), .r(in_6), .in_1(RAM_IN), .out_7(out_24), .out_8(DOUT));
  MEM_BYTE mem_byte_210 (.h(H1), .v(V2), .s(in_4), .e(in_5), .r(in_6), .in_1(RAM_IN), .out_7(out_40), .out_8(DOUT));
  MEM_BYTE mem_byte_211 (.h(H2), .v(V2), .s(in_4), .e(in_5), .r(in_6), .in_1(RAM_IN), .out_7(out_56), .out_8(DOUT));
  MEM_BYTE mem_byte_212 (.h(H3), .v(V2), .s(in_4), .e(in_5), .r(in_6), .in_1(RAM_IN), .out_7(out_72), .out_8(DOUT));
  MEM_BYTE mem_byte_213 (.h(H4), .v(V2), .s(in_4), .e(in_5), .r(in_6), .in_1(RAM_IN), .out_7(out_88), .out_8(DOUT));
  MEM_BYTE mem_byte_214 (.h(H5), .v(V2), .s(in_4), .e(in_5), .r(in_6), .in_1(RAM_IN), .out_7(out_104), .out_8(DOUT));
  MEM_BYTE mem_byte_215 (.h(H6), .v(V2), .s(in_4), .e(in_5), .r(in_6), .in_1(RAM_IN), .out_7(out_120), .out_8(DOUT));
  MEM_BYTE mem_byte_216 (.h(H7), .v(V2), .s(in_4), .e(in_5), .r(in_6), .in_1(RAM_IN), .out_7(out_136), .out_8(DOUT));
  MEM_BYTE mem_byte_217 (.h(H8), .v(V2), .s(in_4), .e(in_5), .r(in_6), .in_1(RAM_IN), .out_7(out_152), .out_8(DOUT));
  MEM_BYTE mem_byte_218 (.h(H9), .v(V2), .s(in_4), .e(in_5), .r(in_6), .in_1(RAM_IN), .out_7(out_168), .out_8(DOUT));
  MEM_BYTE mem_byte_219 (.h(H10), .v(V2), .s(in_4), .e(in_5), .r(in_6), .in_1(RAM_IN), .out_7(out_184), .out_8(DOUT));
  MEM_BYTE mem_byte_220 (.h(H11), .v(V2), .s(in_4), .e(in_5), .r(in_6), .in_1(RAM_IN), .out_7(out_200), .out_8(DOUT));
  MEM_BYTE mem_byte_221 (.h(H12), .v(V2), .s(in_4), .e(in_5), .r(in_6), .in_1(RAM_IN), .out_7(out_216), .out_8(DOUT));
  MEM_BYTE mem_byte_222 (.h(H13), .v(V2), .s(in_4), .e(in_5), .r(in_6), .in_1(RAM_IN), .out_7(out_232), .out_8(DOUT));
  MEM_BYTE mem_byte_223 (.h(H14), .v(V2), .s(in_4), .e(in_5), .r(in_6), .in_1(RAM_IN), .out_7(out_248), .out_8(DOUT));
  MEM_BYTE mem_byte_224 (.h(H15), .v(V2), .s(in_4), .e(in_5), .r(in_6), .in_1(RAM_IN), .out_7(out_264), .out_8(DOUT));
  MEM_BYTE mem_byte_225 (.h(H0), .v(V1), .s(in_4), .e(in_5), .r(in_6), .in_1(RAM_IN), .out_7(out_25), .out_8(DOUT));
  MEM_BYTE mem_byte_226 (.h(H1), .v(V1), .s(in_4), .e(in_5), .r(in_6), .in_1(RAM_IN), .out_7(out_41), .out_8(DOUT));
  MEM_BYTE mem_byte_227 (.h(H2), .v(V1), .s(in_4), .e(in_5), .r(in_6), .in_1(RAM_IN), .out_7(out_57), .out_8(DOUT));
  MEM_BYTE mem_byte_228 (.h(H3), .v(V1), .s(in_4), .e(in_5), .r(in_6), .in_1(RAM_IN), .out_7(out_73), .out_8(DOUT));
  MEM_BYTE mem_byte_229 (.h(H4), .v(V1), .s(in_4), .e(in_5), .r(in_6), .in_1(RAM_IN), .out_7(out_89), .out_8(DOUT));
  MEM_BYTE mem_byte_230 (.h(H5), .v(V1), .s(in_4), .e(in_5), .r(in_6), .in_1(RAM_IN), .out_7(out_105), .out_8(DOUT));
  MEM_BYTE mem_byte_231 (.h(H6), .v(V1), .s(in_4), .e(in_5), .r(in_6), .in_1(RAM_IN), .out_7(out_121), .out_8(DOUT));
  MEM_BYTE mem_byte_232 (.h(H7), .v(V1), .s(in_4), .e(in_5), .r(in_6), .in_1(RAM_IN), .out_7(out_137), .out_8(DOUT));
  MEM_BYTE mem_byte_233 (.h(H8), .v(V1), .s(in_4), .e(in_5), .r(in_6), .in_1(RAM_IN), .out_7(out_153), .out_8(DOUT));
  MEM_BYTE mem_byte_234 (.h(H9), .v(V1), .s(in_4), .e(in_5), .r(in_6), .in_1(RAM_IN), .out_7(out_169), .out_8(DOUT));
  MEM_BYTE mem_byte_235 (.h(H10), .v(V1), .s(in_4), .e(in_5), .r(in_6), .in_1(RAM_IN), .out_7(out_185), .out_8(DOUT));
  MEM_BYTE mem_byte_236 (.h(H11), .v(V1), .s(in_4), .e(in_5), .r(in_6), .in_1(RAM_IN), .out_7(out_201), .out_8(DOUT));
  MEM_BYTE mem_byte_237 (.h(H12), .v(V1), .s(in_4), .e(in_5), .r(in_6), .in_1(RAM_IN), .out_7(out_217), .out_8(DOUT));
  MEM_BYTE mem_byte_238 (.h(H13), .v(V1), .s(in_4), .e(in_5), .r(in_6), .in_1(RAM_IN), .out_7(out_233), .out_8(DOUT));
  MEM_BYTE mem_byte_239 (.h(H14), .v(V1), .s(in_4), .e(in_5), .r(in_6), .in_1(RAM_IN), .out_7(out_249), .out_8(DOUT));
  MEM_BYTE mem_byte_240 (.h(H15), .v(V1), .s(in_4), .e(in_5), .r(in_6), .in_1(RAM_IN), .out_7(out_265), .out_8(DOUT));
  MEM_BYTE mem_byte_241 (.h(H0), .v(V0), .s(in_4), .e(in_5), .r(in_6), .in_1(RAM_IN), .out_7(out_26), .out_8(DOUT));
  MEM_BYTE mem_byte_242 (.h(H1), .v(V0), .s(in_4), .e(in_5), .r(in_6), .in_1(RAM_IN), .out_7(out_42), .out_8(DOUT));
  MEM_BYTE mem_byte_243 (.h(H2), .v(V0), .s(in_4), .e(in_5), .r(in_6), .in_1(RAM_IN), .out_7(out_58), .out_8(DOUT));
  MEM_BYTE mem_byte_244 (.h(H3), .v(V0), .s(in_4), .e(in_5), .r(in_6), .in_1(RAM_IN), .out_7(out_74), .out_8(DOUT));
  MEM_BYTE mem_byte_245 (.h(H4), .v(V0), .s(in_4), .e(in_5), .r(in_6), .in_1(RAM_IN), .out_7(out_90), .out_8(DOUT));
  MEM_BYTE mem_byte_246 (.h(H5), .v(V0), .s(in_4), .e(in_5), .r(in_6), .in_1(RAM_IN), .out_7(out_106), .out_8(DOUT));
  MEM_BYTE mem_byte_247 (.h(H6), .v(V0), .s(in_4), .e(in_5), .r(in_6), .in_1(RAM_IN), .out_7(out_122), .out_8(DOUT));
  MEM_BYTE mem_byte_248 (.h(H7), .v(V0), .s(in_4), .e(in_5), .r(in_6), .in_1(RAM_IN), .out_7(out_138), .out_8(DOUT));
  MEM_BYTE mem_byte_249 (.h(H8), .v(V0), .s(in_4), .e(in_5), .r(in_6), .in_1(RAM_IN), .out_7(out_154), .out_8(DOUT));
  MEM_BYTE mem_byte_250 (.h(H9), .v(V0), .s(in_4), .e(in_5), .r(in_6), .in_1(RAM_IN), .out_7(out_170), .out_8(DOUT));
  MEM_BYTE mem_byte_251 (.h(H10), .v(V0), .s(in_4), .e(in_5), .r(in_6), .in_1(RAM_IN), .out_7(out_186), .out_8(DOUT));
  MEM_BYTE mem_byte_252 (.h(H11), .v(V0), .s(in_4), .e(in_5), .r(in_6), .in_1(RAM_IN), .out_7(out_202), .out_8(DOUT));
  MEM_BYTE mem_byte_253 (.h(H12), .v(V0), .s(in_4), .e(in_5), .r(in_6), .in_1(RAM_IN), .out_7(out_218), .out_8(DOUT));
  MEM_BYTE mem_byte_254 (.h(H13), .v(V0), .s(in_4), .e(in_5), .r(in_6), .in_1(RAM_IN), .out_7(out_234), .out_8(DOUT));
  MEM_BYTE mem_byte_255 (.h(H14), .v(V0), .s(in_4), .e(in_5), .r(in_6), .in_1(RAM_IN), .out_7(out_250), .out_8(DOUT));
  MEM_BYTE mem_byte_256 (.h(H15), .v(V0), .s(in_4), .e(in_5), .r(in_6), .in_1(RAM_IN), .out_7(out_266), .out_8(DOUT));

  assign RAM_ADDR_FLG = RAM_ADDR_IN;
  assign RAM_IN_FLG = RAM_IN;
  assign RAM_OUT_FLG = RAM_OUT;

  // Other names for the same wires on the sheet: DIN[7:0] = RAM_IN; E = in_5; RST = in_6; S = in_4
endmodule

module MEM_BYTE (
  input  [7:0] in_1,
  input  h,
  input  r,
  input  v,
  input  s,
  input  e,
  output [7:0] out_7,
  output [7:0] out_8
);

  wire and_1_out, and_2_out, and_3_out, or_1_out;
  wire [7:0] mem_register_8_1_l_0_c0844130;

  and and_1 (and_1_out, h, v);
  or or_1 (or_1_out, r, and_2_out);
  and and_2 (and_2_out, and_1_out, s);
  and and_3 (and_3_out, and_1_out, e);
  assign out_8 = and_3_out ? mem_register_8_1_l_0_c0844130 : 8'bz;  // Controlled_Buffer controlled_buffer_1
  MEM_REGISTER_8 mem_register_8_1 (
    .i(in_1), .e(or_1_out), .s(and_3_out), .REG(out_7), .L_0_c0844130(mem_register_8_1_l_0_c0844130));
endmodule

module CPU_DEC_4_16 (
  input  [3:0] in_1,
  output L,
  output out_3,
  output out_4,
  output out_5,
  output out_6,
  output out_7,
  output out_8,
  output out_9,
  output out_10,
  output out_11,
  output out_12,
  output out_13,
  output out_14,
  output out_15,
  output out_16,
  output M
);

  wire not_1_out, not_2_out, not_3_out, not_4_out;

  not not_1 (not_1_out, in_1[0]);
  not not_2 (not_2_out, in_1[1]);
  not not_3 (not_3_out, in_1[2]);
  not not_4 (not_4_out, in_1[3]);
  and and_1 (L, not_4_out, not_3_out, not_2_out, not_1_out);
  and and_2 (out_3, not_4_out, not_3_out, not_2_out, in_1[0]);
  and and_3 (out_4, not_4_out, not_3_out, in_1[1], not_1_out);
  and and_4 (out_5, not_4_out, not_3_out, in_1[1], in_1[0]);
  and and_5 (out_6, not_4_out, in_1[2], not_2_out, not_1_out);
  and and_6 (out_7, not_4_out, in_1[2], not_2_out, in_1[0]);
  and and_7 (out_8, not_4_out, in_1[2], in_1[1], not_1_out);
  and and_8 (out_9, not_4_out, in_1[2], in_1[1], in_1[0]);
  and and_9 (out_10, in_1[3], not_3_out, not_2_out, not_1_out);
  and and_10 (out_11, in_1[3], not_3_out, not_2_out, in_1[0]);
  and and_11 (out_12, in_1[3], not_3_out, in_1[1], not_1_out);
  and and_12 (out_13, in_1[3], not_3_out, in_1[1], in_1[0]);
  and and_13 (out_14, in_1[3], in_1[2], not_2_out, not_1_out);
  and and_14 (out_15, in_1[3], in_1[2], not_2_out, in_1[0]);
  and and_15 (out_16, in_1[3], in_1[2], in_1[1], not_1_out);
  and and_16 (M, in_1[3], in_1[2], in_1[1], in_1[0]);

  // Notes on the sheet:
  //   out_13: pull=down
  //   out_14: pull=down
  //   out_15: pull=down
  //   out_16: pull=down
  //   M: pull=down
  //   L: pull=down
  //   out_3: pull=down
  //   out_4: pull=down
  //   out_5: pull=down
  //   out_6: pull=down
  //   out_7: pull=down
  //   out_8: pull=down
  //   out_9: pull=down
  //   out_10: pull=down
  //   out_11: pull=down
  //   out_12: pull=down
  //   in_1: pull=down
endmodule

module MEM_8_BITS (
  input  [7:0] in_1,
  input  s,
  output [7:0] out_3
);

  MEM_LATCH mem_latch_1 (.in_2(s), .in_1(in_1[0]), .out_3(out_3[0]));
  MEM_LATCH mem_latch_2 (.in_2(s), .in_1(in_1[1]), .out_3(out_3[1]));
  MEM_LATCH mem_latch_3 (.in_2(s), .in_1(in_1[2]), .out_3(out_3[2]));
  MEM_LATCH mem_latch_4 (.in_2(s), .in_1(in_1[3]), .out_3(out_3[3]));
  MEM_LATCH mem_latch_5 (.in_2(s), .in_1(in_1[4]), .out_3(out_3[4]));
  MEM_LATCH mem_latch_6 (.in_2(s), .in_1(in_1[5]), .out_3(out_3[5]));
  MEM_LATCH mem_latch_7 (.in_2(s), .in_1(in_1[6]), .out_3(out_3[6]));
  MEM_LATCH mem_latch_8 (.in_2(s), .in_1(in_1[7]), .out_3(out_3[7]));

  // Notes on the sheet:
  //   s: pull=down
  //   out_3: pull=down
  //   in_1: pull=down
endmodule

module MEM_LATCH (
  input  in_1,
  input  in_2,
  output out_3
);

  wire nand_1_out, nand_2_out, nand_4_out;

  nand nand_1 (nand_1_out, in_1, in_2);
  nand nand_2 (nand_2_out, nand_1_out, in_2);
  nand nand_3 (out_3, nand_1_out, nand_4_out);
  nand nand_4 (nand_4_out, out_3, nand_2_out);

  // Notes on the sheet:
  //   in_2: pull=down
  //   in_1: pull=down
endmodule

module FULLADDER (
  input  A,
  input  B,
  input  CI,
  output SUM,
  output CARRY_OUT
);

  wire and_1_out, and_2_out, xor_1_out;

  xor xor_1 (xor_1_out, A, B);
  and and_1 (and_1_out, A, B);
  and and_2 (and_2_out, CI, xor_1_out);
  xor xor_2 (SUM, xor_1_out, CI);
  or or_1 (CARRY_OUT, and_2_out, and_1_out);
endmodule

module ALU_ADDER_8 (
  input  [7:0] in_1,
  input  [7:0] in_2,
  input  in_3,
  output [7:0] out_4,
  output out_5
);

  wire fulladder_1_carry_out, fulladder_2_carry_out, fulladder_3_carry_out, fulladder_4_carry_out,
       fulladder_5_carry_out, fulladder_6_carry_out, fulladder_7_carry_out;

  FULLADDER fulladder_1 (.A(in_1[0]), .B(in_2[0]), .CI(in_3), .SUM(out_4[0]), .CARRY_OUT(fulladder_1_carry_out));
  FULLADDER fulladder_2 (
    .A(in_1[1]), .B(in_2[1]), .CI(fulladder_1_carry_out), .SUM(out_4[1]), .CARRY_OUT(fulladder_2_carry_out));
  FULLADDER fulladder_3 (
    .A(in_1[2]), .B(in_2[2]), .CI(fulladder_2_carry_out), .SUM(out_4[2]), .CARRY_OUT(fulladder_3_carry_out));
  FULLADDER fulladder_4 (
    .A(in_1[3]), .B(in_2[3]), .CI(fulladder_3_carry_out), .SUM(out_4[3]), .CARRY_OUT(fulladder_4_carry_out));
  FULLADDER fulladder_5 (
    .A(in_1[4]), .B(in_2[4]), .CI(fulladder_4_carry_out), .SUM(out_4[4]), .CARRY_OUT(fulladder_5_carry_out));
  FULLADDER fulladder_6 (
    .A(in_1[5]), .B(in_2[5]), .CI(fulladder_5_carry_out), .SUM(out_4[5]), .CARRY_OUT(fulladder_6_carry_out));
  FULLADDER fulladder_7 (
    .A(in_1[6]), .B(in_2[6]), .CI(fulladder_6_carry_out), .SUM(out_4[6]), .CARRY_OUT(fulladder_7_carry_out));
  FULLADDER fulladder_8 (.A(in_1[7]), .B(in_2[7]), .CI(fulladder_7_carry_out), .SUM(out_4[7]), .CARRY_OUT(out_5));
endmodule

module ALU_SHIFT_RIGHT (
  input  [7:0] in_1,
  input  in_2,
  output SHIFT_OUT,
  output [7:0] o
);

  wire [7:1] mem_register_8_1_l_0_c0844130;

  MEM_REGISTER_8 mem_register_8_1 (
    .i(in_1), .e(1'b1), .s(1'b1), .L_0_c0844130({mem_register_8_1_l_0_c0844130, SHIFT_OUT}));  // open: REG
  MEM_REGISTER_8 mem_register_8_2 (
    .i({in_2, mem_register_8_1_l_0_c0844130}), .e(1'b1), .s(1'b1), .L_0_c0844130(o));  // open: REG

  // Notes on the sheet:
  //   SHIFT IN
endmodule

module MEM_REGISTER_8 (
  input  [7:0] i,
  input  e,
  input  s,
  output [7:0] REG,
  output [7:0] L_0_c0844130
);

  wire [7:0] mem_enable_8_1_out_3;

  MEM_8_BITS mem_8_bits_1 (.s(e), .in_1(i), .out_3(REG));
  assign L_0_c0844130 = s ? mem_enable_8_1_out_3 : 8'bz;  // Controlled_Buffer controlled_buffer_1
  MEM_ENABLE_8 mem_enable_8_1 (.in_2(s), .in_1(REG), .out_3(mem_enable_8_1_out_3));

  // Notes on the sheet:
  //   i: pull=down
  //   e: pull=down
  //   s: pull=down
  //   L_0_c0844130: pull=down
endmodule

module MEM_ENABLE_8 (
  input  [7:0] in_1,
  input  in_2,
  output [7:0] out_3
);

  wire and_1_out, and_2_out, and_3_out, and_4_out, and_5_out, and_6_out, and_7_out, and_8_out;

  and and_1 (and_1_out, in_1[0], in_2);
  assign out_3[0] = in_2 ? and_1_out : 1'bz;  // Controlled_Buffer controlled_buffer_1
  and and_2 (and_2_out, in_1[1], in_2);
  assign out_3[1] = in_2 ? and_2_out : 1'bz;  // Controlled_Buffer controlled_buffer_2
  and and_3 (and_3_out, in_1[2], in_2);
  assign out_3[2] = in_2 ? and_3_out : 1'bz;  // Controlled_Buffer controlled_buffer_3
  and and_4 (and_4_out, in_1[3], in_2);
  assign out_3[3] = in_2 ? and_4_out : 1'bz;  // Controlled_Buffer controlled_buffer_4
  and and_5 (and_5_out, in_1[4], in_2);
  assign out_3[4] = in_2 ? and_5_out : 1'bz;  // Controlled_Buffer controlled_buffer_5
  and and_6 (and_6_out, in_1[5], in_2);
  assign out_3[5] = in_2 ? and_6_out : 1'bz;  // Controlled_Buffer controlled_buffer_6
  and and_7 (and_7_out, in_1[6], in_2);
  assign out_3[6] = in_2 ? and_7_out : 1'bz;  // Controlled_Buffer controlled_buffer_7
  and and_8 (and_8_out, in_1[7], in_2);
  assign out_3[7] = in_2 ? and_8_out : 1'bz;  // Controlled_Buffer controlled_buffer_8
endmodule

module ALU_SHIFT_LEFT (
  input  SHIFT_IN,
  input  [7:0] in_2,
  output [7:0] o,
  output out_4
);

  wire [6:0] mem_register_8_1_l_0_c0844130;

  MEM_REGISTER_8 mem_register_8_1 (
    .i(in_2), .e(1'b1), .s(1'b1), .L_0_c0844130({out_4, mem_register_8_1_l_0_c0844130}));  // open: REG
  MEM_REGISTER_8 mem_register_8_2 (
    .i({mem_register_8_1_l_0_c0844130, SHIFT_IN}), .e(1'b1), .s(1'b1), .L_0_c0844130(o));  // open: REG

  // Notes on the sheet:
  //   SHIFT OUT
endmodule

module ALU_LE_COMP (
  input  ABOVE_EQUAL,
  input  A,
  input  A_LARGER,
  input  B,
  output C,
  output A_LARGE,
  output EQUAL
);

  wire and_2_out, not_1_out;

  xor xor_1 (C, A, B);
  not not_1 (not_1_out, C);
  and and_1 (EQUAL, not_1_out, ABOVE_EQUAL);
  and and_2 (and_2_out, ABOVE_EQUAL, A, C);
  or or_1 (A_LARGE, and_2_out, A_LARGER);
endmodule

module ALU_LE_COMP_8 (
  input  [7:0] a,
  input  [7:0] in_2,
  output [7:0] out_3,
  output equal,
  output larger
);

  wire alu_le_comp_1_a_large, alu_le_comp_1_equal, alu_le_comp_2_a_large, alu_le_comp_2_equal,
       alu_le_comp_3_a_large, alu_le_comp_3_equal, alu_le_comp_4_a_large, alu_le_comp_4_equal,
       alu_le_comp_5_a_large, alu_le_comp_5_equal, alu_le_comp_6_a_large, alu_le_comp_6_equal,
       alu_le_comp_7_a_large, alu_le_comp_7_equal;

  ALU_LE_COMP alu_le_comp_1 (
    .ABOVE_EQUAL(1'b1), .A_LARGER(1'b0), .B(in_2[0]), .A(a[0]), .EQUAL(alu_le_comp_1_equal), .C(out_3[7]),
    .A_LARGE(alu_le_comp_1_a_large));
  ALU_LE_COMP alu_le_comp_2 (
    .ABOVE_EQUAL(alu_le_comp_1_equal), .A_LARGER(alu_le_comp_1_a_large), .B(in_2[1]), .A(a[1]),
    .EQUAL(alu_le_comp_2_equal), .C(out_3[6]), .A_LARGE(alu_le_comp_2_a_large));
  ALU_LE_COMP alu_le_comp_3 (
    .ABOVE_EQUAL(alu_le_comp_2_equal), .A_LARGER(alu_le_comp_2_a_large), .B(in_2[2]), .A(a[2]),
    .EQUAL(alu_le_comp_3_equal), .C(out_3[5]), .A_LARGE(alu_le_comp_3_a_large));
  ALU_LE_COMP alu_le_comp_4 (
    .ABOVE_EQUAL(alu_le_comp_3_equal), .A_LARGER(alu_le_comp_3_a_large), .B(in_2[3]), .A(a[3]),
    .EQUAL(alu_le_comp_4_equal), .C(out_3[4]), .A_LARGE(alu_le_comp_4_a_large));
  ALU_LE_COMP alu_le_comp_5 (
    .ABOVE_EQUAL(alu_le_comp_4_equal), .A_LARGER(alu_le_comp_4_a_large), .B(in_2[4]), .A(a[4]),
    .EQUAL(alu_le_comp_5_equal), .C(out_3[3]), .A_LARGE(alu_le_comp_5_a_large));
  ALU_LE_COMP alu_le_comp_6 (
    .ABOVE_EQUAL(alu_le_comp_5_equal), .A_LARGER(alu_le_comp_5_a_large), .B(in_2[5]), .A(a[5]),
    .EQUAL(alu_le_comp_6_equal), .C(out_3[2]), .A_LARGE(alu_le_comp_6_a_large));
  ALU_LE_COMP alu_le_comp_7 (
    .ABOVE_EQUAL(alu_le_comp_6_equal), .A_LARGER(alu_le_comp_6_a_large), .B(in_2[6]), .A(a[6]),
    .EQUAL(alu_le_comp_7_equal), .C(out_3[1]), .A_LARGE(alu_le_comp_7_a_large));
  ALU_LE_COMP alu_le_comp_8 (
    .ABOVE_EQUAL(alu_le_comp_7_equal), .A_LARGER(alu_le_comp_7_a_large), .B(in_2[7]), .A(a[7]),
    .EQUAL(equal), .C(out_3[0]), .A_LARGE(larger));
endmodule

module ALU_DEC_3_8 (
  input  c,
  input  b,
  input  a,
  output [7:0] o
);

  wire not_1_out, not_2_out, not_3_out;

  not not_1 (not_1_out, a);
  not not_2 (not_2_out, b);
  not not_3 (not_3_out, c);
  and and_1 (o[0], not_3_out, not_2_out, not_1_out);
  and and_2 (o[1], not_3_out, not_2_out, a);
  and and_3 (o[2], not_3_out, b, not_1_out);
  and and_4 (o[3], not_3_out, b, a);
  and and_5 (o[4], c, not_2_out, not_1_out);
  and and_6 (o[5], c, not_2_out, a);
  and and_7 (o[6], c, b, not_1_out);
  and and_8 (o[7], c, b, a);

  // Notes on the sheet:
  //   c: pull=down
  //   b: pull=down
  //   a: pull=down
  //   o: pull=down
  //   msb
  //   lsb
endmodule

module ALU_ZERO (
  input  [7:0] i,
  output o
);

  wire or_1_out;

  or or_1 (or_1_out, i[0], i[1], i[2], i[3], i[4], i[5], i[6], i[7]);
  not not_1 (o, or_1_out);
endmodule

module CPU_CLOCK (
  input  CLKIN,
  output CLK,
  output CLKS,
  output CLKE
);

  wire j_k_ff_1_qn, nand_2_out;

  J_K_Flip_Flop j_k_ff_1 (.J(1'b1), .K(1'b1), .clk(CLKIN), .Q(CLK), .Qn(j_k_ff_1_qn));  // open: preset, reset
  nand nand_1 (CLKE, j_k_ff_1_qn, CLKIN);
  nand nand_2 (nand_2_out, CLKIN, CLK);
  not not_1 (CLKS, nand_2_out);
endmodule

module CNTRL_U_STEPPER (
  input  in_1,
  input  in_2,
  output out_3,
  output out_4,
  output out_5,
  output out_6,
  output out_7,
  output out_8,
  output out_9
);

  wire mem_latch_1_out_3, mem_latch_2_out_3, mem_latch_3_out_3, mem_latch_4_out_3, mem_latch_5_out_3,
       mem_latch_6_out_3, mem_latch_7_out_3, mem_latch_8_out_3, mem_latch_9_out_3, mem_latch_10_out_3,
       mem_latch_11_out_3, not_1_out, not_2_out, not_3_out, not_4_out, not_5_out, not_6_out, not_7_out,
       not_8_out, or_1_out, or_2_out;

  not not_1 (not_1_out, in_2);
  not not_2 (not_2_out, in_1);
  or or_1 (or_1_out, in_1, in_2);
  or or_2 (or_2_out, in_1, not_1_out);
  or or_3 (out_3, in_1, not_3_out);
  not not_3 (not_3_out, mem_latch_2_out_3);
  MEM_LATCH mem_latch_1 (.in_2(or_1_out), .in_1(not_2_out), .out_3(mem_latch_1_out_3));
  MEM_LATCH mem_latch_2 (.in_2(or_2_out), .in_1(mem_latch_1_out_3), .out_3(mem_latch_2_out_3));
  and and_1 (out_4, mem_latch_2_out_3, not_4_out);
  not not_4 (not_4_out, mem_latch_4_out_3);
  MEM_LATCH mem_latch_3 (.in_2(or_1_out), .in_1(mem_latch_2_out_3), .out_3(mem_latch_3_out_3));
  MEM_LATCH mem_latch_4 (.in_2(or_2_out), .in_1(mem_latch_3_out_3), .out_3(mem_latch_4_out_3));
  and and_2 (out_5, mem_latch_4_out_3, not_5_out);
  MEM_LATCH mem_latch_5 (.in_2(or_1_out), .in_1(mem_latch_4_out_3), .out_3(mem_latch_5_out_3));
  not not_5 (not_5_out, mem_latch_6_out_3);
  MEM_LATCH mem_latch_6 (.in_2(or_2_out), .in_1(mem_latch_5_out_3), .out_3(mem_latch_6_out_3));
  and and_3 (out_6, mem_latch_6_out_3, not_6_out);
  MEM_LATCH mem_latch_7 (.in_2(or_1_out), .in_1(mem_latch_6_out_3), .out_3(mem_latch_7_out_3));
  not not_6 (not_6_out, mem_latch_8_out_3);
  MEM_LATCH mem_latch_8 (.in_2(or_2_out), .in_1(mem_latch_7_out_3), .out_3(mem_latch_8_out_3));
  and and_4 (out_7, mem_latch_8_out_3, not_7_out);
  not not_7 (not_7_out, mem_latch_10_out_3);
  MEM_LATCH mem_latch_9 (.in_2(or_1_out), .in_1(mem_latch_8_out_3), .out_3(mem_latch_9_out_3));
  MEM_LATCH mem_latch_10 (.in_2(or_2_out), .in_1(mem_latch_9_out_3), .out_3(mem_latch_10_out_3));
  and and_5 (out_8, mem_latch_10_out_3, not_8_out);
  MEM_LATCH mem_latch_11 (.in_2(or_1_out), .in_1(mem_latch_10_out_3), .out_3(mem_latch_11_out_3));
  not not_8 (not_8_out, out_9);
  MEM_LATCH mem_latch_12 (.in_2(or_2_out), .in_1(mem_latch_11_out_3), .out_3(out_9));
endmodule

module CPU_TEMP (
  input  [7:0] i,
  input  s,
  output [7:0] o
);

  wire [7:0] controlled_buffer_1_out;

  assign controlled_buffer_1_out = s ? i : 8'bz;  // Controlled_Buffer controlled_buffer_1
  MEM_8_BITS mem_8_bits_1 (.s(s), .in_1(controlled_buffer_1_out), .out_3(o));

  // Notes on the sheet:
  //   i: pull=down
  //   s: pull=down
  //   o: pull=down
endmodule

module CPU_BUS_1 (
  input  [7:0] i,
  input  bus_1_a6cd2c94,
  output [7:0] o
);

  wire not_1_out;

  and and_1 (o[7], i[7], not_1_out);
  and and_2 (o[6], i[6], not_1_out);
  and and_3 (o[5], i[5], not_1_out);
  and and_4 (o[4], i[4], not_1_out);
  and and_5 (o[3], i[3], not_1_out);
  and and_6 (o[2], i[2], not_1_out);
  and and_7 (o[1], i[1], not_1_out);
  not not_1 (not_1_out, bus_1_a6cd2c94);
  or or_1 (o[0], i[0], bus_1_a6cd2c94);

  // Notes on the sheet:
  //   i: pull=down
  //   o: pull=down
  //   bus_1_a6cd2c94: pull=down
endmodule

module CPU_REG (
  input  [7:0] i,
  input  s,
  input  e,
  output [7:0] \reg ,
  output [7:0] o
);

  MEM_REGISTER_8 mem_register_8_1 (.i(i), .e(s), .s(e), .REG(\reg ), .L_0_c0844130(o));

  // Notes on the sheet:
  //   i: pull=up
  //   s: pull=down
  //   e: pull=down
  //   o: pull=down
endmodule

module CPU_ACCUM (
  input  [7:0] i,
  input  s,
  input  e,
  output [7:0] ACC,
  output [7:0] o
);

  MEM_REGISTER_8 mem_register_8_1 (.i(i), .e(s), .s(e), .REG(ACC), .L_0_c0844130(o));

  // Notes on the sheet:
  //   i: pull=down
  //   s: pull=down
  //   e: pull=down
  //   o: pull=down
endmodule

module CPU_IR (
  input  [7:0] i,
  input  s,
  output [7:0] o
);

  MEM_8_BITS mem_8_bits_1 (.s(s), .in_1(i), .out_3(o));

  // Notes on the sheet:
  //   i: pull=down
  //   s: pull=down
  //   o: pull=down
endmodule

module FLAGS_REG (
  input  in_1,
  input  in_2,
  input  in_3,
  input  in_4,
  input  in_5,
  output out_6,
  output out_7,
  output out_8,
  output out_9
);

  MEM_LATCH mem_latch_1 (.in_2(in_5), .in_1(in_1), .out_3(out_6));
  MEM_LATCH mem_latch_2 (.in_2(in_5), .in_1(in_2), .out_3(out_7));
  MEM_LATCH mem_latch_3 (.in_2(in_5), .in_1(in_3), .out_3(out_8));
  MEM_LATCH mem_latch_4 (.in_2(in_5), .in_1(in_4), .out_3(out_9));
endmodule
